# Fritzing sketch ButtonCircuit (saved by Fritzing 0.9.3b)
breadboards: 1

parts:
  Button = Pushbutton [package="[THT]"]
  Arduino = Arduino Uno (Rev3)
  R1 = Resistor [tolerance=±5% resistance=220 package=THT]

nets:
  N1: Button.Pin_1, Button.Pin_2, Arduino.3V3, R1.Pin_1
  N2: Button.Pin_3, Button.Pin_4, Arduino.D2
  N3: Arduino.GND, R1.Pin_0
