# Fritzing sketch LightRelay (saved by Fritzing 0.9.3b)
breadboards: 1

parts:
  Part1 = Arduino Uno (Rev3) - ICSP
  LED1 = LED - 3mm [color="Red (633nm)" package="3 mm [THT]"]
  R1 = Rotary Potentiometer (Small) [maximum_resistance=100kΩ package=THT]
  R2 = Resistor [tolerance=±5% resistance=220 package="2010 [SMD]"]
  OMRON1 = OMRON PCB Power Relay – G5LE [part_number="G5LE-1\n" package=THT]
  VCC1 = Battery block 9V

nets:
  N1: Part1.GND, OMRON1.COIL2
  N2: Part1.D7, OMRON1.C
  N3: LED1.cathode, VCC1.-
  N4: LED1.anode, R2.Pin_0
  N5: R1.wiper, R2.Pin_1
  N6: R1.leg2, OMRON1.B
  N7: OMRON1.COIL1, VCC1.+
