# Fritzing sketch LightSensor (saved by Fritzing 0.9.3b)
breadboards: 1

parts:
  Arduino = Arduino Uno (Rev3) - ICSP
  Photocell = PHOTOCELL [package=photocell]
  10K_Ohm_Resistor = Resistor [tolerance=±5% resistance=220 package="2010 [SMD]"]

nets:
  N1: Arduino.A0, 10K_Ohm_Resistor.Pin_1
  N2: Arduino.5V, Photocell.P$2
  N3: Photocell.P$1, 10K_Ohm_Resistor.Pin_0
